# Fritzing sketch Extrumento (saved by Fritzing 0.9.3b)
breadboards: 1

parts:
  Funduino_UNO = Arduino Uno (Rev3)
  LCD1 = LCD screen
  LCM1602_IIC1 = LCM1602 IIC [part_number="LCM1602 IIC" chip_label="LCM1602 IIC" package="DIP (Dual Inline) [THT]"]
  S1 = Pushbutton [package="[THT]"]
  S2 = Pushbutton [package="[THT]"]
  R1 = Resistor [tolerance=±5% resistance=10k package=THT]
  R2 = Resistor [tolerance=±5% resistance=10k package=THT]
  M1 = Stepper Motor - Bipolar  # not connected
  C1 = Capacitor Polarized [package=cpol-radial-100uf-25v]
  J1 = ATX24 Pin Power Supply Connector [package=atx24_right_angle]
  DRV_1 = DRV 8825 Stepper Motor Carrier, High Current [part_number="DRV 8825"]  # not connected

nets:
  N1: Funduino_UNO.A4/SDA, LCM1602_IIC1.SDA
  N2: Funduino_UNO.A5/SCL, LCM1602_IIC1.SCL
  GND: Funduino_UNO.GND, LCM1602_IIC1.GND, R1.Pin_0, R2.Pin_0
  N3: Funduino_UNO.D2, S2.Pin_3, S2.Pin_4, R1.Pin_1
  N4: Funduino_UNO.D3_PWM, S1.Pin_3, S1.Pin_4, R2.Pin_1
  5V: Funduino_UNO.5V, LCM1602_IIC1.VCC, S1.Pin_1, S1.Pin_2, S2.Pin_1, S2.Pin_2
  VSS: LCD1.VSS, LCM1602_IIC1.VSS
  VDD: LCD1.VDD, LCM1602_IIC1.VDD
  N5: LCD1.V0, LCM1602_IIC1.V0
  N6: LCD1.RS, LCM1602_IIC1.RS
  N7: LCD1.R/W, LCM1602_IIC1.RW
  N8: LCD1.E, LCM1602_IIC1.E
  N9: LCD1.DB0, LCM1602_IIC1.D0
  N10: LCD1.DB1, LCM1602_IIC1.D1
  N11: LCD1.DB2, LCM1602_IIC1.D2
  N12: LCD1.DB3, LCM1602_IIC1.D3
  N13: LCD1.DB4, LCM1602_IIC1.D4
  N14: LCD1.DB5, LCM1602_IIC1.D5
  N15: LCD1.DB6, LCM1602_IIC1.D6
  N16: LCD1.DB7, LCM1602_IIC1.D7
  N17: LCD1.LED+, LCM1602_IIC1.A
  N18: LCD1.LED-, LCM1602_IIC1.K
  N19: C1.+, J1.12V
  N20: C1.-, J1.GND

custom parts:
  LCM1602 IIC: I2C-Module to use a 1602 or 2004 LCD on with the wire.h libory Serial LCD Modul
